# Fritzing sketch C_LEDanDigitalemPin (saved by Fritzing 0.9.2b)
circuit board: 8.46667cm x 5.64444cm
breadboards: 1

parts:
  Bauteil1 = Arduino Nano (Rev3.0)
  R1 = Resistor [tolerance=±5% resistance=220 package=THT]
  LED1 = smd LED [color="Green (555nm)" package="0805 [SMD]"]

nets (from the pcb view):
  N1: Bauteil1.GND, LED1.cathode
  N2: Bauteil1.5V, R1.Pin_0
  N3: R1.Pin_1, LED1.anode
