# Fritzing sketch F_FernbedienungSchaltetLED (saved by Fritzing 0.9.2b)
circuit board: 8.46667cm x 5.64444cm
breadboards: 1

parts:
  Bauteil1 = Arduino Nano (Rev3.0)
  R2 = Resistor [tolerance=±5% resistance=220 package=THT]
  LED2 = smd LED [color="Green (555nm)" package="0805 [SMD]"]
  Bauteil2 = Max Power IR LED Kit

nets:
  N1: Bauteil1.GND, LED2.cathode
  N2: Bauteil1.D2, R2.Pin_0
  N3: Bauteil1.D5, Bauteil2.CONTROL
  5V: Bauteil1.5V, Bauteil2.VCC
  N4: R2.Pin_1, LED2.anode
