# Fritzing sketch H_Servo (saved by Fritzing 0.9.2b)
circuit board: 8.46667cm x 5.64444cm
breadboards: 1

parts:
  Bauteil1 = Arduino Nano (Rev3.0)
  J1 = Basic Servo

nets:
  N1: Bauteil1.D5, J1.pulse
  5V: Bauteil1.5V, J1.vcc
