# Fritzing sketch J_Lautsprecher (saved by Fritzing 0.9.2b)
circuit board: 8.46667cm x 5.64444cm
breadboards: 1

parts:
  Bauteil1 = Arduino Nano (Rev3.0)
  J1 = Piezo Speaker

nets:
  N1: Bauteil1.GND, J1.pin1
  N2: Bauteil1.D5, J1.pin2
