# Fritzing sketch F_SchalterZaehlerNichtEntprellt (saved by Fritzing 0.9.2b)
circuit board: 8.46667cm x 5.64444cm
breadboards: 1

parts:
  Bauteil1 = Arduino Nano (Rev3.0)
  S1 = Pushbutton [package="[THT]"]

nets:
  N1: Bauteil1.GND, S1.Pin_1, S1.Pin_2
  N2: Bauteil1.D2, S1.Pin_3, S1.Pin_4
