# Fritzing sketch 07-servo-ansteuern (saved by Fritzing 0.9.3b)
circuit board: 8.46667cm x 5.64444cm
breadboards: 1

parts:
  Bauteil1 = Arduino Nano (Rev3.0)
  J1 = Basic Servo
  VCC1 = 4 x AAA Battery Mount

nets:
  GND: Bauteil1.GND, J1.gnd, VCC1.-
  N1: Bauteil1.D5, J1.pulse
  N2: J1.vcc, VCC1.+
