# Fritzing sketch 08-lichtsensor-benutzen (saved by Fritzing 0.9.2b)
circuit board: 8.46667cm x 5.64444cm
breadboards: 1

parts:
  Bauteil1 = Arduino Nano (Rev3.0)
  R1 = PHOTOCELL [package=photocell]
  R2 = Resistor [tolerance=±5% resistance=1k package="0805 [SMD]"]

nets:
  N1: Bauteil1.GND, R2.Pin_0
  N2: Bauteil1.A0, R1.P$1, R2.Pin_1
