# Fritzing sketch 09-lichtsensor-steuert-led (saved by Fritzing 0.9.2b)
circuit board: 8.46667cm x 5.64444cm
breadboards: 1

parts:
  Bauteil1 = Arduino Nano (Rev3.0)
  R2 = Resistor [tolerance=±5% resistance=1k package="0805 [SMD]"]
  R1 = PHOTOCELL [package=photocell]
  R4 = Resistor [tolerance=±5% resistance=220 package=THT]
  LED2 = smd LED [color="White (6500K)" package="0805 [SMD]"]

nets:
  N1: Bauteil1.GND, R2.Pin_0, LED2.cathode
  N2: Bauteil1.D2, R4.Pin_1
  N3: Bauteil1.5V, R1.P$2
  N4: Bauteil1.A0, R2.Pin_1, R1.P$1
  N5: R4.Pin_0, LED2.anode
