# Fritzing sketch 10-abstand-einlesen (saved by Fritzing 0.9.3b)
circuit board: 8.46667cm x 5.64444cm
breadboards: 1

parts:
  Bauteil1 = Arduino Nano (Rev3.0)
  VCC1 = 4 x AAA Battery Mount
  hc-sr1 = hc-sr04

nets:
  GND: Bauteil1.GND, VCC1.-, hc-sr1.GND
  N1: Bauteil1.D9, hc-sr1.Trig
  N2: Bauteil1.D10, hc-sr1.Echo
