# Fritzing sketch 12-motor-ansteuern (saved by Fritzing 0.9.3b)
circuit board: 8.46667cm x 5.64444cm
breadboards: 2

parts:
  Bauteil1 = Arduino Nano (Rev3.0)
  M2 = DC Motor
  S2 = H-Bridge with L298N
  VCC2 = Battery block 9V

nets:
  GND: Bauteil1.GND, S2.GND, VCC2.-
  N1: Bauteil1.D7, S2.IN3
  N2: Bauteil1.D8, S2.IN4
  N3: Bauteil1.D9, S2.ENB
  N4: M2.pin_1, S2.M2-02
  N5: M2.pin_2, S2.M2-01
  N6: S2.12V, VCC2.+

custom parts:
  H-Bridge with L298N: h-bridge
