# Fritzing sketch 16-elektrische-leitfaehigkeit-messen (saved by Fritzing 0.9.3b)
circuit board: 8.46667cm x 5.64444cm
breadboards: 1

parts:
  Bauteil1 = Arduino Nano (Rev3.0)
  LED1 = smd LED [color="Green (555nm)" package="0805 [SMD]"]
  LED2 = smd LED [color="Red (633nm)" package="0805 [SMD]"]
  Part3 = FC-28 Soil Hygrometer Module - Probe
  Part4 = FC-28 Soil Hygrometer Module
  S3 = H-Bridge with L298N
  VCC3 = Battery block 9V
  R2 = Resistor [tolerance=±5% resistance=220 package=THT]
  R3 = Resistor [tolerance=±5% resistance=220 package=THT]

nets:
  GND: Bauteil1.GND, LED1.cathode, LED2.cathode, Part4.GND, S3.GND, VCC3.-
  N1: Bauteil1.D2, R2.Pin_1
  N2: Bauteil1.D3, R3.Pin_1
  N3: Bauteil1.A0, Part4.AO
  N4: LED1.anode, R2.Pin_0
  N5: LED2.anode, R3.Pin_0
  N6: Part3.POS, Part4.POS
  N7: Part3.NEG, Part4.NEG
  VCC: Part4.VCC, S3.5V
  N8: S3.12V, VCC3.+

custom parts:
  FC-28 Soil Hygrometer Module - Probe: The FC-28 is a soil hygrometer module that uses the Texas Instruments LM393 comparator chip to provide an analog measurement of soil humidity.
  FC-28 Soil Hygrometer Module: The FC-28 is a soil hygrometer module that uses the Texas Instruments LM393 comparator chip to provide an analog measurement of soil humidity. The digital output is high when soil moisture is over a certain threshold, as determined by adjusting the potentiometer.
  H-Bridge with L298N: h-bridge
