# Fritzing sketch G_Feuchtigkeitssensor (saved by Fritzing 0.9.2b)
circuit board: 8.46667cm x 5.64444cm
breadboards: 1

parts:
  Bauteil1 = Arduino Nano (Rev3.0)
  LED1 = smd LED [color="Green (555nm)" package="0805 [SMD]"]
  LED2 = smd LED [color="Red (633nm)" package="0805 [SMD]"]
  Part3 = FC-28 Soil Hygrometer Module - Probe
  Part4 = FC-28 Soil Hygrometer Module
  R6 = Resistor [tolerance=±5% resistance=220 package=THT]
  R7 = Resistor [tolerance=±5% resistance=220 package=THT]

nets:
  N1: Bauteil1.GND, LED1.cathode, LED2.cathode
  N2: Bauteil1.D2, R7.Pin_1
  N3: Bauteil1.D3, R6.Pin_1
  5V: Bauteil1.5V, Part4.VCC
  N4: Bauteil1.A0, Part4.AO
  N5: LED1.anode, R7.Pin_0
  N6: LED2.anode, R6.Pin_0
  N7: Part3.POS, Part4.NEG
  N8: Part3.NEG, Part4.POS

custom parts:
  FC-28 Soil Hygrometer Module - Probe: The FC-28 is a soil hygrometer module that uses the Texas Instruments LM393 comparator chip to provide an analog measurement of soil humidity.
  FC-28 Soil Hygrometer Module: The FC-28 is a soil hygrometer module that uses the Texas Instruments LM393 comparator chip to provide an analog measurement of soil humidity. The digital output is high when soil moisture is over a certain threshold, as determined by adjusting the potentiometer.
