# Fritzing sketch ButtonPullDownExtern (saved by Fritzing 0.9.2b)
breadboards: 1

parts:
  Bauteil1 = Arduino Nano (Rev3.0)
  S1 = Momentary Switch [package=ksa_sealed_tac_switch]
  R1 = Resistor [tolerance=±5% resistance=10k package="0402 [SMD]"]

nets:
  N1: Bauteil1.GND, R1.Pin_0
  N2: Bauteil1.D2, S1.3, R1.Pin_1
  N3: Bauteil1.5V, S1.1

// code stored in the sketch: ButtonPullup.ino
void setup(){
   Serial.begin(9600);
}

int a = 0;
void loop(){
  Serial.println(a++); 
}
