# Fritzing sketch ButtonPullupIntern (saved by Fritzing 0.9.2b)
breadboards: 1

parts:
  Bauteil1 = Arduino Nano (Rev3.0)
  S1 = Momentary Switch [package=ksa_sealed_tac_switch]

nets:
  N1: Bauteil1.GND, S1.1
  N2: Bauteil1.D2, S1.3

// code stored in the sketch: ButtonPullup.ino
void setup(){
   Serial.begin(9600);
}

int a = 0;
void loop(){
  Serial.println(a++); 
}
